// Logisim project Digital Dice.circ as structural Verilog: 1 circuit, main circuit main
module main (
);

  wire and_1_out, and_2_out, and_3_out, and_4_out, and_5_out, and_6_out, and_7_out, and_8_out, and_9_out,
       button_1_out, nor_1_out, not_1_out, not_2_out, not_3_out, not_4_out, not_5_out, not_6_out, not_7_out,
       not_8_out, or_1_out, or_2_out, or_3_out, or_4_out;
  wire [2:0] random_1_out;

  Button button_1 (.out(button_1_out));
  or or_1 (or_1_out, and_9_out, nor_1_out);
  Random #(.width(3)) random_1 (.clk(button_1_out), .out(random_1_out), .clr(or_1_out));  // open: next
  not not_1 (not_1_out, random_1_out[2]);
  not not_2 (not_2_out, random_1_out[1]);
  not not_3 (not_3_out, random_1_out[0]);
  not not_4 (not_4_out, random_1_out[1]);
  not not_5 (not_5_out, random_1_out[0]);
  not not_6 (not_6_out, random_1_out[0]);
  not not_7 (not_7_out, random_1_out[2]);
  not not_8 (not_8_out, random_1_out[1]);
  and and_1 (and_1_out, not_1_out, random_1_out[1]);
  and and_2 (and_2_out, random_1_out[2], not_2_out);
  and and_3 (and_3_out, random_1_out[1], not_3_out);
  and and_4 (and_4_out, random_1_out[2], not_4_out);
  and and_5 (and_5_out, random_1_out[2], not_5_out);
  and and_6 (and_6_out, random_1_out[2], random_1_out[1], not_6_out);
  and and_7 (and_7_out, not_7_out, random_1_out[0]);
  and and_8 (and_8_out, not_8_out, random_1_out[0]);
  and and_9 (and_9_out, random_1_out[0], random_1_out[1], random_1_out[2]);
  nor nor_1 (nor_1_out, random_1_out[2], random_1_out[1], random_1_out[0]);
  or or_2 (or_2_out, and_1_out, and_2_out, and_3_out);
  or or_3 (or_3_out, and_4_out, and_5_out);
  or or_4 (or_4_out, and_7_out, and_8_out);
  LED led_1 (.in(or_2_out));
  LED led_2 (.in(and_6_out));
  LED led_3 (.in(or_4_out));
  LED led_4 (.in(or_3_out));
  LED led_5 (.in(or_3_out));
  LED led_6 (.in(and_6_out));
  LED led_7 (.in(or_2_out));
  Hex_Digit_Display hex_digit_display_1 (.value({1'b0, random_1_out}));  // open: dp

  // Notes on the sheet:
  //   23BCE505 - Dev Solanki
  //   Innovative Assignment 
  //   " Digital Dice "
  //   23BCE517 - Akshat Jingar
endmodule
